# Fritzing sketch Esquemático fritzing (saved by Fritzing 1.0.5)

parts:
  A1 = ESP32-S3-1-N16R8-module
  LCD1 = 2.8" SPI TFT Module [part_number=MSP2807]

nets:
  N1: A1.Pin_1, LCD1.pin1, LCD1.pin8
  N2: A1.Pin_19, LCD1.pin13
  N3: A1.Pin_21, A1.Pin_22, LCD1.pin2, LCD1.pin14
  N4: A1.Pin_23, LCD1.pin11
  N5: A1.Pin_24, LCD1.pin3
  N6: A1.Pin_25, LCD1.pin4
  N7: A1.Pin_34, LCD1.pin12
  N8: A1.Pin_35, LCD1.pin6
  N9: A1.Pin_36, LCD1.pin7
  N10: A1.Pin_37, LCD1.pin10
  N11: A1.Pin_38, LCD1.pin5

custom parts:
  ESP32-S3-1-N16R8-module: ESP32-S3 CAM development board WiFi Bluetooth module onboard ESP32-S3-1 N16R8 module dual TYPE-C interface.
  2.8" SPI TFT Module: A generic 2.8 inch LCD TFT 320x240 display with touchscreen and SD card slot. Uses the ILI9341 controller, like the Adafruit displays of this size uses.
